# Fritzing sketch AdvancedTimer (saved by Fritzing 0.9.9b)
breadboards: 1

parts:
  Arduino_Nano = Arduino Nano (Rev3.0)
  Rotary_Encoder = ENCODER_2LED [package=encoder_led_2]
  LED_matrix = LED Matrix - Serial Interface - Red/Green/Blue
  VCC1 = Battery block 9V
  PW_SWTCH = Toggle Switch [package=THT]

nets:
  GND: Arduino_Nano.GND, Rotary_Encoder.-, LED_matrix.GND, PW_SWTCH.L2
  N1: Arduino_Nano.D2, Rotary_Encoder.+R
  N2: Arduino_Nano.D3, Rotary_Encoder.+G
  N3: Arduino_Nano.D4, Rotary_Encoder.SW
  N4: Arduino_Nano.D10, LED_matrix.CS
  N5: Arduino_Nano.D11/MOSI, LED_matrix.MOSI
  N6: Arduino_Nano.VIN, VCC1.+
  5V: Arduino_Nano.5V, Rotary_Encoder.A, LED_matrix.VCC
  N7: Arduino_Nano.D13/SCK, LED_matrix.SCK
  N8: VCC1.-, PW_SWTCH.COM
